# Fritzing sketch circuit (saved by Fritzing 0.9.3b)
breadboards: 1

parts:
  Parça1 = Arduino Uno (Rev3)
  U1 = LCD-16X2 [package=lcd-16x2]
  M1 = Stepper Motor - Bipolar
  IR1 = TSOP312.., 314.. [package=THT]
  R1 = Rotary Potentiometer (Small) [maximum_resistance=100kΩ package=THT]
  U2 = LIPO-1000mAh [package=lipo-1000]
  D1 = Rectifier Diode [part_number=N5399 package="Melf DO-213 AB [SMD]"]
  C1 = Electrolytic Capacitor [capacitance=0.22mF package="100 mil [THT, electrolytic]"]
  HLK-PM3 = HLK-PM01
  D2 = Rectifier Diode [part_number=N5399 package="Melf DO-213 AB [SMD]"]
  D4 = Rectifier Diode [part_number=N5399 package="Melf DO-213 AB [SMD]"]
  D3 = Rectifier Diode [part_number=N5399 package="Melf DO-213 AB [SMD]"]
  S1 = SWITCH-MOMENTARY-2 [package=tactile-switch-1101ne]
  R1_2 = Resistor [tolerance=±5% resistance=10k package="0805 [SMD]"]
  R2 = Resistor [tolerance=±5% resistance=100k package="0805 [SMD]"]
  C2 = Electrolytic Capacitor [capacitance=0.22mF package="100 mil [THT, electrolytic]"]
  D5 = Rectifier Diode [part_number=N5399 package="Melf DO-213 AB [SMD]"]
  D6 = Rectifier Diode [part_number=N5399 package="Melf DO-213 AB [SMD]"]
  D7 = Rectifier Diode [part_number=N5399 package="Melf DO-213 AB [SMD]"]
  D8 = Rectifier Diode [part_number=N5399 package="Melf DO-213 AB [SMD]"]

nets:
  N1: Parça1.A0, R1_2.Pin_1, R2.Pin_0
  N2: Parça1.D12/MISO, U1.E
  N3: Parça1.D13/SCK, U1.RS
  GND: Parça1.GND, U1.VSS, U1.R_W, U1.K, IR1.GND, R1.leg1, R1_2.Pin_0
  N4: Parça1.D2, IR1.Data
  N5: Parça1.D3_PWM, U1.DB7
  N6: Parça1.D4, U1.DB6
  N7: Parça1.D5_PWM, U1.DB5
  N8: Parça1.D6_PWM, U1.DB4
  5V: Parça1.5V, U1.VDD, U1.A, IR1.Vs, R1.leg2
  N9: Parça1.VIN, U2.+, HLK-PM3.+Vo
  N10: U1.VO, R1.wiper
  N11: M1.A, S1.2, D6.anode, D7.cathode
  N12: M1.C, D2.cathode, D4.anode
  N13: M1.B, S1.1
  N14: M1.D, D1.anode, D3.cathode
  N15: U2.-, HLK-PM3.-Vo
  N16: D1.cathode, C1.+, HLK-PM3.AC#1, D4.cathode
  N17: C1.-, HLK-PM3.AC#0, D2.anode, D3.anode
  N18: R2.Pin_1, C2.+, D6.cathode, D8.cathode
  N19: C2.-, D5.anode, D7.anode
  N20: D5.cathode, D8.anode
